# Fritzing sketch schema (saved by Fritzing 0.9.2b)
circuit board: 8.46667cm x 5.64444cm
breadboards: 1

parts:
  Part1 = Arduino Uno (Rev3) - ICSP
  LED2 = LED - 3mm [color="Red (633nm)" package="3 mm [THT]"]
  LED1 = LED - 3mm [color="Yellow (595nm)" package="3 mm [THT]"]
  LED4 = LED - 3mm [color="White (4500K)" package="3 mm [THT]"]
  LED3 = LED - 3mm [color="Green (555nm)" package="3 mm [THT]"]
  R1 = Resistor [tolerance=±5% resistance=330 package="0603 [SMD]"]
  R2 = Resistor [tolerance=±5% resistance=330 package="0603 [SMD]"]
  R3 = Resistor [tolerance=±5% resistance=330 package="0603 [SMD]"]
  R4 = Resistor [tolerance=±5% resistance=330 package="0603 [SMD]"]
  S4 = Pushbutton [package="[THT]"]
  S3 = Pushbutton [package="[THT]"]
  S2 = Pushbutton [package="[THT]"]
  S1 = Pushbutton [package="[THT]"]

nets:
  N1: Part1.D10_PWM/SS, S1.Pin_3, S1.Pin_4
  N2: Part1.D11_PWM/MOSI, S2.Pin_3, S2.Pin_4
  N3: Part1.D12/MISO, S3.Pin_3, S3.Pin_4
  N4: Part1.D13/SCK, S4.Pin_3, S4.Pin_4
  N5: Part1.D3_PWM, LED1.anode
  N6: Part1.D4, LED2.anode
  N7: Part1.D5_PWM, LED3.anode, R3.Pin_0
  N8: Part1.D6_PWM, LED4.anode
  N9: Part1.GND, R1.Pin_1, R2.Pin_1, R3.Pin_1, R4.Pin_1, S4.Pin_1, S4.Pin_2, S3.Pin_1, S3.Pin_2, S2.Pin_1, S2.Pin_2, S1.Pin_1, S1.Pin_2
  N10: LED2.cathode, R2.Pin_0
  N11: LED1.cathode, R1.Pin_0
  N12: LED4.cathode, R4.Pin_0
